// Logisim project M2 - ULA.circ as structural Verilog: 14 circuits, main circuit ULA_Funcional
module Meio_Somador (
  input  A,
  input  B,
  output SOMA,
  output TS
);

  xor xor_1 (SOMA, A, B);
  and and_1 (TS, B, A);
endmodule

module Somado_Completo (
  input  A,
  input  B,
  input  Te,
  output S,
  output Ts
);

  wire and_1_out, and_2_out, and_3_out, xor_1_out;

  xor xor_1 (xor_1_out, A, B);
  xor xor_2 (S, xor_1_out, Te);
  and and_1 (and_1_out, B, Te);
  or or_1 (Ts, and_1_out, and_2_out, and_3_out);
  and and_2 (and_2_out, Te, A);
  and and_3 (and_3_out, B, A);
endmodule

module Somador_de_4_Bits (
  input  A3,
  input  B3,
  input  A2,
  input  B2,
  input  A1,
  input  B1,
  input  A0,
  input  B0,
  output S3,
  output S2,
  output S1,
  output S0,
  output S4
);

  wire meio_somador_1_ts, somado_completo_1_ts, somado_completo_2_ts, somado_completo_3_ts;

  xor xor_1 (S4, somado_completo_1_ts, somado_completo_2_ts);
  Somado_Completo somado_completo_1 (.B(B3), .Te(somado_completo_2_ts), .S(S3), .Ts(somado_completo_1_ts), .A(A3));
  Somado_Completo somado_completo_2 (.B(B2), .Te(somado_completo_3_ts), .S(S2), .Ts(somado_completo_2_ts), .A(A2));
  Somado_Completo somado_completo_3 (.B(B1), .Te(meio_somador_1_ts), .S(S1), .Ts(somado_completo_3_ts), .A(A1));
  Meio_Somador meio_somador_1 (.A(A0), .B(B0), .SOMA(S0), .TS(meio_somador_1_ts));
endmodule

module Meio_Subtrator (
  input  A,
  input  B,
  output S,
  output TS
);

  wire not_1_out;

  xor xor_1 (S, A, B);
  not not_1 (not_1_out, A);
  and and_1 (TS, not_1_out, B);
endmodule

module Subtrator_Completo (
  input  in_1,
  input  in_2,
  input  in_3,
  output S,
  output TS
);

  wire and_1_out, and_2_out, and_3_out, not_1_out, xor_1_out;

  not not_1 (not_1_out, in_1);
  xor xor_1 (xor_1_out, in_1, in_2);
  and and_1 (and_1_out, not_1_out, in_2);
  and and_2 (and_2_out, not_1_out, in_3);
  and and_3 (and_3_out, in_2, in_3);
  xor xor_2 (S, xor_1_out, in_3);
  or or_1 (TS, and_1_out, and_2_out, and_3_out);
endmodule

module Subtrator_de_4_Bits (
  input  A3,
  input  B3,
  input  A2,
  input  B2,
  input  A1,
  input  B1,
  input  A0,
  input  B0,
  output S3,
  output S2,
  output S1,
  output S0,
  output S4
);

  wire meio_subtrator_1_ts, subtrator_completo_1_ts, subtrator_completo_2_ts, subtrator_completo_3_ts;

  xor xor_1 (S4, subtrator_completo_1_ts, subtrator_completo_2_ts);
  Subtrator_Completo subtrator_completo_1 (
    .in_1(A3), .in_2(B3), .in_3(subtrator_completo_2_ts), .S(S3), .TS(subtrator_completo_1_ts));
  Subtrator_Completo subtrator_completo_2 (
    .in_1(A2), .in_2(B2), .in_3(subtrator_completo_3_ts), .S(S2), .TS(subtrator_completo_2_ts));
  Subtrator_Completo subtrator_completo_3 (
    .in_1(A1), .in_2(B1), .in_3(meio_subtrator_1_ts), .S(S1), .TS(subtrator_completo_3_ts));
  Meio_Subtrator meio_subtrator_1 (.A(A0), .B(B0), .S(S0), .TS(meio_subtrator_1_ts));
endmodule

module Incrementador_de_4_Bits (
  input  A3,
  input  A2,
  input  A1,
  input  A0,
  input  Um,
  output S3,
  output S2,
  output S1,
  output S0,
  output C
);

  wire meio_somador_1_ts, meio_somador_2_ts, meio_somador_3_ts, meio_somador_4_ts;

  Meio_Somador meio_somador_1 (.A(A3), .B(meio_somador_2_ts), .SOMA(S3), .TS(meio_somador_1_ts));
  xor xor_1 (C, meio_somador_1_ts, meio_somador_2_ts);
  Meio_Somador meio_somador_2 (.A(A2), .B(meio_somador_3_ts), .SOMA(S2), .TS(meio_somador_2_ts));
  Meio_Somador meio_somador_3 (.A(A1), .B(meio_somador_4_ts), .SOMA(S1), .TS(meio_somador_3_ts));
  Meio_Somador meio_somador_4 (.A(A0), .B(Um), .SOMA(S0), .TS(meio_somador_4_ts));
endmodule

module Decrementador_de_4_Bits (
  input  A3,
  input  A2,
  input  A1,
  input  A0,
  input  UM,
  output S3,
  output S2,
  output S1,
  output S0,
  output C
);

  wire meio_subtrator_1_ts, meio_subtrator_2_ts, meio_subtrator_3_ts, meio_subtrator_4_ts;

  Meio_Subtrator meio_subtrator_1 (.A(A3), .B(meio_subtrator_2_ts), .S(S3), .TS(meio_subtrator_1_ts));
  xor xor_1 (C, meio_subtrator_1_ts, meio_subtrator_2_ts);
  Meio_Subtrator meio_subtrator_2 (.A(A2), .B(meio_subtrator_3_ts), .S(S2), .TS(meio_subtrator_2_ts));
  Meio_Subtrator meio_subtrator_3 (.A(A1), .B(meio_subtrator_4_ts), .S(S1), .TS(meio_subtrator_3_ts));
  Meio_Subtrator meio_subtrator_4 (.A(A0), .B(UM), .S(S0), .TS(meio_subtrator_4_ts));
endmodule

module Pass (
  input  in_1,
  input  in_2,
  input  in_3,
  input  in_4,
  output [3:0] out_5
);


  assign out_5 = {in_1, in_2, in_3, in_4};
endmodule

module ULA_Tentativa1 (
  input  [3:0] B,
  input  [3:0] A,
  input  [2:0] in_3,
  output Overflow_Flag,
  output Zero_Flag,
  output [3:0] out_6,
  output Sinal
);

  wire decrementador_de_4_bits_1_c, incrementador_de_4_bits_1_c, somador_de_4_bits_1_s4,
       subtrator_de_4_bits_1_s4;
  wire [3:0] and_1_out, complemento_2_1_out_3, complemento_2_2_out_3, decrementador_de_4_bits_1_s0,
       incrementador_de_4_bits_1_s0, multiplexer_1_out, not_1_out, or_1_out, pass_1_out_5,
       somador_de_4_bits_1_s0, subtrator_de_4_bits_1_s0;

  Pass pass_1 (.in_1(A[3]), .in_2(A[2]), .in_3(A[1]), .in_4(A[0]), .out_5(pass_1_out_5));
  Complemento_2 complemento_2_1 (.in_1(A), .out_3(complemento_2_1_out_3));  // open: out_2
  Hex_Digit_Display hex_digit_display_1 (.value(complemento_2_1_out_3));  // open: dp
  Decrementador_de_4_Bits decrementador_de_4_bits_1 (
    .A3(A[3]), .A2(A[2]), .A1(A[1]), .A0(A[0]), .UM(B[0]), .C(decrementador_de_4_bits_1_c),
    .S3(decrementador_de_4_bits_1_s0[3]), .S2(decrementador_de_4_bits_1_s0[2]),
    .S1(decrementador_de_4_bits_1_s0[1]), .S0(decrementador_de_4_bits_1_s0[0]));
  Complemento_2 complemento_2_2 (.in_1(B), .out_3(complemento_2_2_out_3));  // open: out_2
  Hex_Digit_Display hex_digit_display_2 (.value(complemento_2_2_out_3));  // open: dp
  Incrementador_de_4_Bits incrementador_de_4_bits_1 (
    .A3(A[3]), .A2(A[2]), .A1(A[1]), .A0(A[0]), .Um(B[0]), .C(incrementador_de_4_bits_1_c),
    .S3(incrementador_de_4_bits_1_s0[3]), .S2(incrementador_de_4_bits_1_s0[2]),
    .S1(incrementador_de_4_bits_1_s0[1]), .S0(incrementador_de_4_bits_1_s0[0]));
  Multiplexer #(.select(3), .width(4), .enable("false")) multiplexer_1 (
    .in0(pass_1_out_5), .in1(decrementador_de_4_bits_1_s0), .in2(incrementador_de_4_bits_1_s0),
    .in3(somador_de_4_bits_1_s0), .in4(subtrator_de_4_bits_1_s0), .in5(not_1_out), .in6(or_1_out),
    .in7(and_1_out), .out(multiplexer_1_out), .sel(in_3));
  Complemento_2 complemento_2_3 (.in_1(multiplexer_1_out), .out_2(Sinal), .out_3(out_6));
  Somador_de_4_Bits somador_de_4_bits_1 (
    .A3(A[3]), .B3(B[3]), .A2(A[2]), .B2(B[2]), .A1(A[1]), .B1(B[1]), .A0(A[0]), .B0(B[0]),
    .S2(somador_de_4_bits_1_s0[2]), .S1(somador_de_4_bits_1_s0[1]), .S0(somador_de_4_bits_1_s0[0]),
    .S3(somador_de_4_bits_1_s0[3]), .S4(somador_de_4_bits_1_s4));
  Overflow_Flag overflow_flag_1 (
    .in_1(decrementador_de_4_bits_1_c), .in_2(incrementador_de_4_bits_1_c), .in_3(somador_de_4_bits_1_s4),
    .in_4(subtrator_de_4_bits_1_s4), .in_5(in_3), .Overflow_Flag(Overflow_Flag));
  Zero_Flag zero_flag_1 (.in_1(multiplexer_1_out), .Zero_Flag(Zero_Flag));
  Subtrator_de_4_Bits subtrator_de_4_bits_1 (
    .A3(A[3]), .B3(B[3]), .A2(A[2]), .B2(B[2]), .A1(A[1]), .B1(B[1]), .A0(A[0]), .B0(B[0]),
    .S2(subtrator_de_4_bits_1_s0[2]), .S1(subtrator_de_4_bits_1_s0[1]), .S0(subtrator_de_4_bits_1_s0[0]),
    .S3(subtrator_de_4_bits_1_s0[3]), .S4(subtrator_de_4_bits_1_s4));
  assign not_1_out = ~A;  // NOT_Gate not_1, 4 bits wide
  assign or_1_out = A | B;  // OR_Gate or_1, 4 bits wide
  assign and_1_out = A & B;  // AND_Gate and_1, 4 bits wide
endmodule

module Complemento_2 (
  input  [3:0] in_1,
  output out_2,
  output [3:0] out_3
);

  wire [3:0] decrementador_de_4_bits_1_s0, not_1_out;

  Decrementador_de_4_Bits decrementador_de_4_bits_1 (
    .A3(in_1[3]), .A2(in_1[2]), .A1(in_1[1]), .A0(in_1[0]), .UM(in_1[3]),
    .S3(decrementador_de_4_bits_1_s0[3]), .S2(decrementador_de_4_bits_1_s0[2]),
    .S1(decrementador_de_4_bits_1_s0[1]), .S0(decrementador_de_4_bits_1_s0[0]));  // open: C
  assign not_1_out = ~decrementador_de_4_bits_1_s0;  // NOT_Gate not_1, 4 bits wide
  Multiplexer #(.width(4), .enable("false")) multiplexer_1 (
    .in0(decrementador_de_4_bits_1_s0), .in1(not_1_out), .out(out_3), .sel(in_1[3]));

  assign out_2 = in_1[3];
endmodule

module Zero_Flag (
  input  [3:0] in_1,
  output Zero_Flag
);

  wire [3:0] multiplexer_1_out, not_1_out, not_2_out;

  assign not_1_out = ~in_1;  // NOT_Gate not_1, 4 bits wide
  Multiplexer #(.select(4), .width(4), .enable("false")) multiplexer_1 (
    .in0(not_1_out), .in1(in_1), .in2(in_1), .in3(in_1), .in4(in_1), .in5(in_1), .in6(in_1), .in7(in_1),
    .in8(in_1), .in9(in_1), .in10(in_1), .in11(in_1), .in12(in_1), .in13(in_1), .in14(in_1),
    .in15(not_2_out), .out(multiplexer_1_out), .sel(in_1));
  assign not_2_out = ~in_1;  // NOT_Gate not_2, 4 bits wide
  and and_1 (Zero_Flag, multiplexer_1_out[0], multiplexer_1_out[1], multiplexer_1_out[2], multiplexer_1_out[3]);
endmodule

module ULA_Funcional (
  input  [3:0] in_1,
  input  [3:0] in_2,
  input  [2:0] in_3,
  output out_4,
  output out_5,
  output out_6,
  output out_7,
  output out_8
);

  wire [3:0] complemento_2_1_out_3, complemento_2_2_out_3, ula_tentativa1_1_out_6;

  Complemento_2 complemento_2_1 (.in_1(in_1), .out_2(out_4), .out_3(complemento_2_1_out_3));
  Hex_Digit_Display hex_digit_display_1 (.value(complemento_2_1_out_3));  // open: dp
  Hex_Digit_Display hex_digit_display_2 (.value(complemento_2_2_out_3));  // open: dp
  Hex_Digit_Display hex_digit_display_3 (.value(ula_tentativa1_1_out_6));  // open: dp
  Complemento_2 complemento_2_2 (.in_1(in_2), .out_2(out_5), .out_3(complemento_2_2_out_3));
  ULA_Tentativa1 ula_tentativa1_1 (
    .in_3(in_3), .Sinal(out_8), .Overflow_Flag(out_6), .Zero_Flag(out_7), .A(in_1),
    .out_6(ula_tentativa1_1_out_6), .B(in_2));
endmodule

module Overflow_Flag (
  input  in_1,
  input  in_2,
  input  in_3,
  input  in_4,
  input  [2:0] in_5,
  output Overflow_Flag
);

  Multiplexer #(.select(3), .enable("false")) multiplexer_1 (
    .in1(in_1), .in2(in_2), .in3(in_3), .in4(in_4), .out(Overflow_Flag), .sel(in_5));  // open: in0, in5, in6, in7
endmodule
